# Fritzing sketch pedsignal (saved by Fritzing 0.9.2b)
circuit board: 8.46667cm x 5.64444cm
breadboards: 1

parts:
  R1 = Resistor [tolerance=±5% resistance=220 package=THT]
  LED_MSG_PUSH = LED - 5mm [color="Orange (620nm)" package="5 mm [THT]"]
  LED_MSG_WAIT = LED - 5mm [color="Orange (620nm)" package="5 mm [THT]"]
  LED_CAR_RED = LED - 5mm [color="Red (633nm)" package="5 mm [THT]"]
  LED_PED_BLUE = LED - 5mm [color="Green (570nm)" package="5 mm [THT]"]
  LED_PED_RED = LED - 5mm [color="Red (633nm)" package="5 mm [THT]"]
  LED_CAR_YEL = LED - 5mm [color="Yellow (595nm)" package="5 mm [THT]"]
  LED_CAR_BLUE = LED - 5mm [color="Green (570nm)" package="5 mm [THT]"]
  R2 = Resistor [tolerance=±5% resistance=220 package=THT]
  R3 = Resistor [tolerance=±5% resistance=220 package=THT]
  R4 = Resistor [tolerance=±5% resistance=220 package=THT]
  R5 = Resistor [tolerance=±5% resistance=220 package=THT]
  R6 = Resistor [tolerance=±5% resistance=220 package=THT]
  R7 = Resistor [tolerance=±5% resistance=220 package=THT]
  PB_PED_ABROAD = Pushbutton [package="[THT]"]
  Raspberry_Pi1 = Raspberry Pi B rev2

nets:
  N1: R1.Pin_0, LED_MSG_PUSH.anode
  N2: R1.Pin_1, Raspberry_Pi1.GPIO_22
  N3: LED_MSG_PUSH.cathode, LED_MSG_WAIT.cathode, LED_CAR_RED.cathode, LED_PED_BLUE.cathode, LED_PED_RED.cathode, LED_CAR_YEL.cathode, LED_CAR_BLUE.cathode, PB_PED_ABROAD.Pin_3, PB_PED_ABROAD.Pin_4, Raspberry_Pi1.GND
  N4: LED_MSG_WAIT.anode, R2.Pin_0
  N5: LED_CAR_RED.anode, R3.Pin_0
  N6: LED_PED_BLUE.anode, R4.Pin_0
  N7: LED_PED_RED.anode, R5.Pin_0
  N8: LED_CAR_YEL.anode, R6.Pin_0
  N9: LED_CAR_BLUE.anode, R7.Pin_0
  N10: R2.Pin_1, Raspberry_Pi1.GPIO_27
  N11: R3.Pin_1, Raspberry_Pi1.GPIO_18
  N12: R4.Pin_1, Raspberry_Pi1.GPIO_17
  N13: R5.Pin_1, Raspberry_Pi1.GPIO_4
  N14: R6.Pin_1, Raspberry_Pi1.GPIO_3
  N15: R7.Pin_1, Raspberry_Pi1.GPIO_2
  N16: PB_PED_ABROAD.Pin_1, PB_PED_ABROAD.Pin_2, Raspberry_Pi1.GPIO_24
